# Fritzing sketch Shipment Warning System Circuit Diagram (saved by Fritzing 0.9.3b)
breadboards: 1

parts:
  HC-SR04_Sensor_1 = HC-SR04 Ultrasonic Distance Sensor
  HC-SR04_Sensor_2 = HC-SR04 Ultrasonic Distance Sensor
  Q2 = npn-Powertransistor [package="TO220 [THT]"]
  R1 = Resistor [tolerance=±5% resistance=1k package="0603 [SMD]"]
  Q3 = npn-Powertransistor [package="TO220 [THT]"]
  R3 = Resistor [tolerance=±5% resistance=1k package="0603 [SMD]"]
  LED1 = smd LED [color="Red (633nm)" package="1206 [SMD]"]
  LED3 = smd LED [color="Yellow (595nm)" package="1206 [SMD]"]
  U2 = NodeMCU V1.0

nets:
  VCC: HC-SR04_Sensor_1.VCC, HC-SR04_Sensor_2.VCC
  N1: HC-SR04_Sensor_1.TRIG, U2.D2
  N2: HC-SR04_Sensor_1.ECHO, U2.D1
  GND: HC-SR04_Sensor_1.GND, HC-SR04_Sensor_2.GND
  N3: HC-SR04_Sensor_2.TRIG, U2.D6
  N4: HC-SR04_Sensor_2.ECHO, U2.D5
  N5: Q2.base, R3.Pin_1
  N6: Q2.collector, LED1.cathode
  N7: Q2.emitter, Q3.emitter
  N8: R1.Pin_0, Q3.base
  N9: R1.Pin_1, U2.D7
  N10: Q3.collector, LED3.cathode
  N11: R3.Pin_0, U2.D3
  N12: LED1.anode, LED3.anode

notes:
  Dolu Kutu Işığı
  Boş Kutu Işığı
  Dolu Kutu Sensörü
  Boş Kutu Sensörü
  5V
  12V

custom parts:
  NodeMCU V1.0: ESP8266 based NodeMCU V1.0
